# Fritzing sketch Masimo_schema (saved by Fritzing 0.9.3b)
breadboards: 1

parts:
  Part1 = Arduino Uno (Rev3)
  S1 = Pushbutton [package="[THT]"]
  R1 = Resistor [tolerance=±5% resistance=220 package=THT]
  R2 = Rotary Potentiometer (Small) [maximum_resistance=100kΩ package=THT]
  S2 = Pushbutton [package="[THT]"]
  R3 = Resistor [tolerance=±5% resistance=220 package=THT]
  LED1 = LED - 5mm [color="Red (633nm)" package="5 mm [THT]"]
  Injectori_i_Pumpa = DC Motor
  Q1 = Basic FET N-Channel [package="DPak [SMD]"]
  VCC1 = Battery  # not connected
  R4 = Resistor [tolerance=±5% resistance=330 package=THT]
  U1 = RELAY-2 [package=relay-g5v]

nets:
  N1: Part1.A2, R2.wiper
  N2: Part1.D13/SCK, LED1.anode, Q1.Gate
  N3: Part1.D2, S1.Pin_1, S1.Pin_2, S1.Pin_3, S1.Pin_4, R1.Pin_1
  N4: Part1.D5_PWM, S2.Pin_1, S2.Pin_2, S2.Pin_3, S2.Pin_4, R3.Pin_1
  N5: Part1.5V, R2.leg2
  N6: Part1.GND, R1.Pin_0, R2.leg1, R3.Pin_0, Injectori_i_Pumpa.pin_2, Q1.source, R4.Pin_1, U1.1
  N7: Part1.VIN, U1.5
  N8: LED1.cathode, R4.Pin_0
  N9: Injectori_i_Pumpa.pin_1, U1.6
  N10: Q1.drain, U1.10
