# Fritzing sketch schema (saved by Fritzing 0.9.3b)
breadboards: 1

parts:
  Part1 = Arduino Uno (Rev3)
  S1 = Pushbutton [package="[THT]"]
  S2 = Pushbutton [package="[THT]"]
  S3 = Pushbutton [package="[THT]"]
  S4 = Pushbutton [package="[THT]"]
  S5 = Pushbutton [package="[THT]"]
  R1 = Resistor [tolerance=±5% resistance=2.2k package=THT]
  R2 = Resistor [tolerance=±5% resistance=2.2k package=THT]
  R3 = Resistor [tolerance=±5% resistance=2.2k package=THT]
  R4 = Resistor [tolerance=±5% resistance=2.2k package=THT]
  R5 = Resistor [tolerance=±5% resistance=2.2k package=THT]
  LED1 = LED - 5mm [color="Green (555nm)" package="5 mm [THT]"]
  LED2 = LED - 5mm [color="Green (555nm)" package="5 mm [THT]"]
  LED3 = LED - 5mm [color="Green (555nm)" package="5 mm [THT]"]
  LED4 = LED - 5mm [color="Green (555nm)" package="5 mm [THT]"]
  R6 = Resistor [tolerance=±5% resistance=330 package=THT]
  R7 = Resistor [tolerance=±5% resistance=330 package=THT]
  R8 = Resistor [tolerance=±5% resistance=330 package=THT]
  R9 = Resistor [tolerance=±5% resistance=330 package=THT]
  LED5 = LED - 5mm [color="Red (633nm)" package="5 mm [THT]"]
  R10 = Resistor [tolerance=±5% resistance=330 package=THT]
  part = Basic FET N-Channel [package="TO220 [THT]"]
  Q3 = Basic FET N-Channel [package="TO220 [THT]"]
  Q4 = Basic FET N-Channel [package="TO220 [THT]"]
  Q5 = Basic FET N-Channel [package="TO220 [THT]"]
  Q6 = Basic FET N-Channel [package="TO220 [THT]"]
  Injector_1 = DC Motor
  Injector_2 = DC Motor
  Injector_3 = DC Motor
  Injector_4 = DC Motor
  Pump = DC Motor

nets:
  N1: Part1.D10_PWM/SS, S5.Pin_1, S5.Pin_2, S5.Pin_3, S5.Pin_4, R2.Pin_1
  N2: Part1.D11_PWM/MOSI, S4.Pin_1, S4.Pin_2, S4.Pin_3, S4.Pin_4
  N3: Part1.D12/MISO, S3.Pin_1, S3.Pin_2, S3.Pin_3, S3.Pin_4, R4.Pin_1
  N4: Part1.D13/SCK, S2.Pin_1, S2.Pin_2, S2.Pin_3, S2.Pin_4, R5.Pin_1
  N5: Part1.GND, R1.Pin_0, R2.Pin_0, R3.Pin_0, R4.Pin_0, R5.Pin_0, R6.Pin_1, R7.Pin_1, R8.Pin_1, R9.Pin_1, R10.Pin_1, part.source, Q3.source, Q4.source, Q5.source, Q6.source, Injector_1.pin_2, Injector_2.pin_2, Injector_3.pin_2, Injector_4.pin_2, Pump.pin_2
  N6: Part1.D2, S1.Pin_1, S1.Pin_2, S1.Pin_3, S1.Pin_4, R1.Pin_1
  N7: Part1.D3_PWM, LED5.anode, Q6.gate
  N8: Part1.D4, LED3.anode, Q5.gate
  N9: Part1.D5_PWM, LED2.anode, Q4.gate
  N10: Part1.D6_PWM, LED1.anode, Q3.gate
  N11: Part1.D7, LED4.anode, part.gate
  N12: LED1.cathode, R8.Pin_0
  N13: LED2.cathode, R7.Pin_0
  N14: LED3.cathode, R6.Pin_0
  N15: LED4.cathode, R9.Pin_0
  N16: LED5.cathode, R10.Pin_0
